# Fritzing sketch big button testing (saved by Fritzing 0.9.3b)

parts:
  U2 = NodeMCU V3.0
  Part7 = Analog Digital MUX Breakout
  S3 = Round Pushbutton
  R1 = Resistor [tolerance=±5% resistance=10k package="1206 [SMD]"]

nets:
  N1: U2.D0, Part7.S3
  N2: U2.D4, Part7.S2
  3V3: U2.3V3, Part7.VCC, S3.leg1, R1.Pin_1
  GND: U2.GND, Part7.GND, Part7.EN, R1.Pin_0
  N3: U2.D6, Part7.SIG
  N4: U2.D7, Part7.S1
  N5: U2.D8, Part7.S0
  N6: Part7.C15, S3.leg0

custom parts:
  NodeMCU V3.0: ESP8266 based NodeMCU
