# Fritzing sketch block_diagram (saved by Fritzing 0.9.3b)
breadboards: 1
perfboards: 1

parts:
  U1 = NodeMCU V3.0
  8_Channel_Relay1 = 8 Channel Power Relay
  M2 = DC Motor
  M3 = DC Motor
  M4 = DC Motor
  M5 = DC Motor
  M6 = DC Motor
  M1 = DC Motor
  BAT1 = BC9VPC [package=bc9vpc]
  Load_Cell2 = Load Cell - Red/white/black/green
  Part5 = HX711 Weighing Sensor Module
  Part6 = Analog Digital MUX Breakout
  LCD1 = LCD screen
  LCM1602_IIC1 = LCM1602 IIC [part_number="LCM1602 IIC" chip_label="LCM1602 IIC" package="DIP (Dual Inline) [THT]"]
  Part7 = Breadboard Power Supply Board SMD
  ENCODER1 = Rotary Encoder with Knob
  S2 = Round Pushbutton
  U2 = NodeMCU V3.0
  J1 = female pin header, 2 pins [form="♀ (female)"]  # not connected
  J2 = female pin header, 2 pins [form="♀ (female)"]  # not connected
  J3 = female pin header, 2 pins [form="♀ (female)"]  # not connected
  J4 = female pin header, 2 pins [form="♀ (female)"]  # not connected
  J5 = female pin header, 15 pins [form="♀ (female)"]  # not connected
  J6 = female pin header, 15 pins [form="♀ (female)"]  # not connected
  Part8 = Analog Digital MUX Breakout  # not connected
  J7 = female pin header, 16 pins [form="♀ (female)"]  # not connected
  J8 = female pin header, 8 pins [form="♀ (female)"]  # not connected
  J9 = female pin header, 6 pins [form="♀ (female)"]  # not connected
  J10 = female pin header, 4 pins [form="♀ (female)"]  # not connected
  Part9 = HX711 Weighing Sensor Module  # not connected
  R2 = Resistor [tolerance=±5% resistance=10k package="1206 [SMD]"]  # not connected
  R4 = Resistor [tolerance=±5% resistance=10k package="1206 [SMD]"]

nets:
  N1: U1.D0, Part6.S3
  N2: U1.D1, LCM1602_IIC1.SCL
  N3: U1.D2, LCM1602_IIC1.SDA
  N4: U1.D3, Part5.CK/TX
  N5: U1.D4, Part6.S2
  VCC: U1.3V3, Part5.VCC, Part6.VCC, ENCODER1.no_name_yet#4, R4.Pin_1
  N6: U1.D5, Part5.DO/RX
  N7: U1.D6, Part6.SIG
  N8: U1.D7, Part6.S1
  N9: U1.D8, Part6.S0
  GND: U1.GND, 8_Channel_Relay1.GND, M2.pin_1, M3.pin_1, M4.pin_1, M5.pin_1, M6.pin_1, M1.pin_1, BAT1.V-, Part5.GND, Part6.GND, Part6.EN, LCM1602_IIC1.GND, Part7.GND, ENCODER1.no_name_yet#5, S2.leg1, R4.Pin_0
  VCC_2: U1.Vin, 8_Channel_Relay1.VCC, 8_Channel_Relay1.JD-VCC, LCM1602_IIC1.VCC, Part7.VCC
  N10: 8_Channel_Relay1.IN1, Part6.C0
  N11: 8_Channel_Relay1.IN2, Part6.C1
  N12: 8_Channel_Relay1.IN3, Part6.C2
  N13: 8_Channel_Relay1.IN4, Part6.C3
  N14: 8_Channel_Relay1.IN5, Part6.C4
  N15: 8_Channel_Relay1.IN6, Part6.C5
  N16: 8_Channel_Relay1.IN7, Part6.C6
  N17: 8_Channel_Relay1.IN8, Part6.C7
  N18: 8_Channel_Relay1.COM, BAT1.V+, Part7.VIN
  N19: 8_Channel_Relay1.NO#23, M1.pin_2
  N20: 8_Channel_Relay1.NO#26, M2.pin_2
  N21: 8_Channel_Relay1.NO#29, M3.pin_2
  N22: 8_Channel_Relay1.NO#32, M4.pin_2
  N23: 8_Channel_Relay1.NO#35, M5.pin_2
  N24: 8_Channel_Relay1.NO#38, M6.pin_2
  N25: Load_Cell2.wire1, Part5.E+
  N26: Load_Cell2.wire2, Part5.E-
  N27: Load_Cell2.wire3, Part5.A+
  N28: Load_Cell2.wire4, Part5.A-
  N29: Part6.C12, ENCODER1.no_name_yet#1
  N30: Part6.C13, ENCODER1.no_name_yet#2
  N31: Part6.C14, ENCODER1.no_name_yet#3
  N32: Part6.C15, S2.leg0
  VSS: LCD1.VSS, LCM1602_IIC1.VSS
  VDD: LCD1.VDD, LCM1602_IIC1.VDD
  N33: LCD1.V0, LCM1602_IIC1.V0
  N34: LCD1.RS, LCM1602_IIC1.RS
  N35: LCD1.R/W, LCM1602_IIC1.RW
  N36: LCD1.E, LCM1602_IIC1.E
  N37: LCD1.DB0, LCM1602_IIC1.D0
  N38: LCD1.DB1, LCM1602_IIC1.D1
  N39: LCD1.DB2, LCM1602_IIC1.D2
  N40: LCD1.DB3, LCM1602_IIC1.D3
  N41: LCD1.DB4, LCM1602_IIC1.D4
  N42: LCD1.DB5, LCM1602_IIC1.D5
  N43: LCD1.DB6, LCM1602_IIC1.D6
  N44: LCD1.DB7, LCM1602_IIC1.D7
  N45: LCD1.LED+, LCM1602_IIC1.A
  N46: LCD1.LED-, LCM1602_IIC1.K
  N47: LCM1602_IIC1.LED_A, LCM1602_IIC1.LED_B
  N48: U2.GND#6, U2.GND#13, U2.GND#16, U2.GND#33

notes:
  Power to Arduino with USB connector
  Power to Adapter with barrel connector
  ↑ GND VCC
  ↓ SW DT CLK
  3V3 short circuit?
  ←Reversed
  connections

custom parts:
  NodeMCU V3.0: ESP8266 based NodeMCU
  8 Channel Power Relay: An 8 channel power relay. The module operates at 5V.
  Load Cell - Red/white/black/green: A rectangle load cell/weighting pressure Sensor with four wires - Red, white, black, green. Normally corresponding with E+, E-, A+, A- respectively.
  LCM1602 IIC: I2C-Module to use a 1602 or 2004 LCD on with the wire.h libory Serial LCD Modul
  Rotary Encoder with Knob: Rotary Encoder with 1/4" Shaft and Knob
