# Fritzing sketch coffee_control_panel (saved by Fritzing 0.9.3b)

parts:
  R2 = Resistor [tolerance=±5% resistance=222k package=THT]
  R1 = Resistor [tolerance=±1% resistance=390 package=THT]
  R3 = Resistor [tolerance=±1% resistance=390 package=THT]
  S1 = Momentary Switch [package=ksa_sealed_tac_switch]
  S2 = Momentary Switch [package=ksa_sealed_tac_switch]
  S3 = Momentary Switch [package=ksa_sealed_tac_switch]
  S4 = Momentary Switch [package=ksa_sealed_tac_switch]
  LED1 = LED - 5mm [color="Green (555nm)" package="5 mm [THT]"]
  LED2 = LED - 5mm [color="Green (555nm)" package="5 mm [THT]"]
  S5 = Momentary Switch [package=ksa_sealed_tac_switch]
  S6 = Momentary Switch [package=ksa_sealed_tac_switch]
  LED3 = LED - 5mm [color="Green (555nm)" package="5 mm [THT]"]
  LED4 = LED - 5mm [color="Green (555nm)" package="5 mm [THT]"]
  LED5 = LED - 5mm [color="Green (555nm)" package="5 mm [THT]"]
  LED6 = LED - 5mm [color="Red (633nm)" package="5 mm [THT]"]
  J1 = female pin header, 4 pins [form="♀ (female)"]
  J2 = female pin header, 3 pins [form="♀ (female)"]

nets:
  N1: R2.Pin_0, S1.1, S1.2, S2.2, LED1.cathode, LED2.cathode
  N2: R2.Pin_1, R3.Pin_0, J2.pin2
  N3: R1.Pin_0, J1.pin2
  N4: R1.Pin_1, LED1.anode, LED3.anode, LED5.anode
  N5: R3.Pin_1, LED2.anode, LED4.anode, LED6.anode
  N6: S1.3, S1.4, S3.3, S3.4, S5.3, J1.pin1
  N7: S2.1, J1.pin3
  N8: S2.3, S2.4, S4.3, S4.4, S6.3, S6.4, J2.pin3
  N9: S3.1, S3.2, S4.2, LED3.cathode
  N10: S4.1, LED4.cathode, J1.pin4
  N11: S5.1, S6.2, LED5.cathode, LED6.cathode, J2.pin1

notes:
  1  2  3  4
  5  6  7
  5-, 7+
  5-, 1+
  4-, 7+, 2+
  1-, 2+
  7+, 3-, 2+
  1- , 2+, 5-
  -  -  +
  +  +   -   -
  2 = VIN?
  6 = GND?
