# Fritzing sketch rotary multiplexer testing (saved by Fritzing 0.9.3b)

parts:
  R6 = Resistor [tolerance=±5% resistance=10k package="1206 [SMD]"]  # not connected
  U4 = NodeMCU V3.0
  Part11 = Analog Digital MUX Breakout
  ENCODER2 = Rotary Encoder with Knob

nets:
  N1: U4.D0, Part11.S3
  N2: U4.D4, Part11.S2
  3V3: U4.3V3, Part11.VCC, ENCODER2.no_name_yet#4
  GND: U4.GND, Part11.GND, Part11.EN, ENCODER2.no_name_yet#5
  N3: U4.D6, Part11.SIG
  N4: U4.D7, Part11.S1
  N5: U4.D8, Part11.S0
  N6: Part11.C12, ENCODER2.no_name_yet#1
  N7: Part11.C13, ENCODER2.no_name_yet#2
  N8: Part11.C14, ENCODER2.no_name_yet#3

notes:
  ↑ GND VCC
  ↓ SW DT CLK
  Yes connections are really reversed

custom parts:
  NodeMCU V3.0: ESP8266 based NodeMCU
  Rotary Encoder with Knob: Rotary Encoder with 1/4" Shaft and Knob
