# Fritzing sketch weight sensor testing (saved by Fritzing 0.9.3b)

parts:
  U2 = NodeMCU V3.0
  Part6 = HX711 Weighing Sensor Module
  Load_Cell3 = Load Cell - Red/white/black/green

nets:
  N1: U2.D3, Part6.CK/TX
  3V3: U2.3V3, Part6.VCC
  GND: U2.GND, Part6.GND
  N2: U2.D5, Part6.DO/RX
  N3: Part6.E+, Load_Cell3.wire1
  N4: Part6.E-, Load_Cell3.wire2
  N5: Part6.A+, Load_Cell3.wire3
  N6: Part6.A-, Load_Cell3.wire4

custom parts:
  NodeMCU V3.0: ESP8266 based NodeMCU
  Load Cell - Red/white/black/green: A rectangle load cell/weighting pressure Sensor with four wires - Red, white, black, green. Normally corresponding with E+, E-, A+, A- respectively.
